// Logisim project micro.circ as structural Verilog: 1 circuit, main circuit EV20_Superescalar
module EV20_Superescalar (
);

  wire button_1_out, undriven_2;
  wire [9:0] undriven;

  Button button_1 (.out(button_1_out));
  Pipeline_register pipeline_register_1 (
    .S_low_P_high(1'b0), .CLK(button_1_out), .Serial_IN({32{1'b1}}), .D_Address_IN(10'h2aa), .Hold(1'b0));  // open: ALUC_IN, SH_IN, Kmx_IN, MRyMB_IN, B_bus_IN, T_bus_IN, C_bus_IN, A_bus_IN, ALUC_OUT, SH_OUT, Kmx_OUT, MRyMB_OUT, B_bus_OUT, T_bus_OUT, C_bus_OUT, Serial_OUT, A_bus_OUT, D_Address_OUT
  Pipeline_register LoadStore (
    .S_low_P_high(1'b0), .CLK(button_1_out), .D_Address_IN(undriven), .Hold(1'b0));  // open: ALUC_IN, SH_IN, Kmx_IN, MRyMB_IN, B_bus_IN, T_bus_IN, C_bus_IN, Serial_IN, A_bus_IN, ALUC_OUT, SH_OUT, Kmx_OUT, MRyMB_OUT, B_bus_OUT, T_bus_OUT, C_bus_OUT, Serial_OUT, A_bus_OUT, D_Address_OUT
  Pipeline_register ALU (
    .S_low_P_high(1'b0), .CLK(button_1_out), .Hold(1'b0));  // open: ALUC_IN, SH_IN, Kmx_IN, MRyMB_IN, B_bus_IN, T_bus_IN, C_bus_IN, Serial_IN, A_bus_IN, D_Address_IN, ALUC_OUT, SH_OUT, Kmx_OUT, MRyMB_OUT, B_bus_OUT, T_bus_OUT, C_bus_OUT, Serial_OUT, A_bus_OUT, D_Address_OUT
  Register #(.width(16)) register_1 ();  // open: D, en, Q, clk, clr
  Register #(.width(16)) La (.en(undriven_2), .clk(button_1_out));  // open: D, Q, clr
  Register #(.width(16)) Lb (.en(undriven_2), .clk(button_1_out));  // open: D, Q, clr
endmodule
